# Fritzing sketch bme280_bb (saved by Fritzing 0.9.3b)
stripboards: 1

parts:
  S1 = Pushbutton [package="[SMD]"]
  J3 = double row male pin header, 4 pins [form="♂ (male)"]
  J1 = shrouded pin header, 26 pins [form="♂ (shrouded male)"]
  J2 = double row male pin header, 4 pins [form="♂ (male)"]
  J4 = shrouded pin header, 26 pins [form="♂ (shrouded male)"]
  J5 = double row male pin header, 4 pins [form="♂ (male)"]
  J6 = double row male pin header, 4 pins [form="♂ (male)"]
  S2 = Pushbutton [package="[THT]"]
  LED3 = LED - 3mm [color="Red (633nm)" package="3 mm [THT]"]
  R2 = Resistor [tolerance=±5% resistance=330 package=THT]

nets:
  N1: S1.Pin_1, S1.Pin_2, J3.pin3, J1.pin17, J2.pin2, J4.pin17, J5.pin2, J6.pin3, S2.Pin_3, S2.Pin_4, R2.Pin_1
  N2: S1.Pin_3, S1.Pin_4, J1.pin22, J4.pin22, S2.Pin_1, S2.Pin_2
  N3: J3.pin1, J1.pin2, J2.pin4, J4.pin2, J5.pin4, J6.pin1
  N4: J3.pin2, J1.pin3, J2.pin3, J4.pin3, J5.pin3, J6.pin2
  N5: J3.pin4, J1.pin9, J2.pin1, J4.pin9, J5.pin1, J6.pin4
  N6: J1.pin1, J4.pin1
  N7: J1.pin4, J4.pin4
  N8: J1.pin5, J4.pin5
  N9: J1.pin6, J4.pin6
  N10: J1.pin7, J4.pin7
  N11: J1.pin8, J4.pin8
  N12: J1.pin10, J4.pin10
  N13: J1.pin11, J4.pin11
  N14: J1.pin12, J4.pin12
  N15: J1.pin13, J4.pin13
  N16: J1.pin14, J4.pin14
  N17: J1.pin15, J4.pin15
  N18: J1.pin16, J4.pin16
  N19: J1.pin18, J4.pin18
  N20: J1.pin19, J4.pin19
  N21: J1.pin20, J4.pin20
  N22: J1.pin21, J4.pin21
  N23: J1.pin23, J4.pin23, LED3.anode
  N24: J1.pin24, J4.pin24
  N25: J1.pin25, J4.pin25
  N26: J1.pin26, J4.pin26
  N27: LED3.cathode, R2.Pin_0
